// Logisim project trabalho_2.circ as structural Verilog: 6 circuits, main circuit PC_e_MI
module trabalho (
);

  wire ALUSrc, and_1_out, Branch, clk, MemtoReg, RegWr, Zero;
  wire [1:0] ALUOp;
  wire [7:0] bit_extender_1_out, multiplexer_1_out, multiplexer_2_out, pc_e_mi_1_out_6, pc_e_mi_1_out_7, rs1,
       rs2, ula_1_out_5;

  and and_1 (and_1_out, Zero, Branch);
  Clock clock_1 (.out(clk));
  PC_e_MI pc_e_mi_1 (
    .addr(rs2), .Branch(and_1_out), .r2(rs2), .clk(clk), .d(rs1), .out_6(pc_e_mi_1_out_6),
    .out_7(pc_e_mi_1_out_7));
  Multiplexer #(.width(8)) multiplexer_1 (
    .in0(ula_1_out_5), .in1(pc_e_mi_1_out_7), .out(multiplexer_1_out), .sel(MemtoReg));
  unidade_de_controle unidade_de_controle_1 (
    .in_1(pc_e_mi_1_out_6[7:4]), .ALUOp(ALUOp), .ALUSrc(ALUSrc), .Branch(Branch), .RegWr(RegWr),
    .MemtoReg(MemtoReg));
  banco_de_registradores banco_de_registradores_1 (
    .Dado(multiplexer_1_out), .RegWrite(RegWr), .rs2(pc_e_mi_1_out_6[1:0]), .rs1(pc_e_mi_1_out_6[3:2]),
    .ALUSrc(ALUSrc), .clk(clk), .saida_2(rs2), .saida_1(rs1));  // open: Reset
  assign bit_extender_1_out = {{4{pc_e_mi_1_out_6[3]}}, pc_e_mi_1_out_6[3:0]};  // Bit_Extender bit_extender_1
  Multiplexer #(.width(8)) multiplexer_2 (.in0(rs2), .in1(bit_extender_1_out), .out(multiplexer_2_out), .sel(ALUSrc));
  ULA ula_1 (.rs2(multiplexer_2_out), .rs1(rs1), .ALUOp(ALUOp), .zero(Zero), .out_5(ula_1_out_5));
endmodule

module PC_e_MI (
  input  [7:0] addr,
  input  Branch,
  input  [7:0] r2,
  input  clk,
  input  [7:0] d,
  output [7:0] out_6,
  output [7:0] out_7
);

  wire and_1_out, button_1_out;
  wire [7:0] adder_1_out, multiplexer_1_out, register_1_q;

  Adder adder_1 (.a(register_1_q), .b(8'h1), .out(adder_1_out), .cin(1'b0));  // open: cout
  Register register_1 (.D(adder_1_out), .en(1'b1), .clk(clk), .Q(register_1_q), .clr(button_1_out));
  Button button_1 (.out(button_1_out));
  Multiplexer #(.width(8)) multiplexer_1 (.in0(register_1_q), .in1(r2), .out(multiplexer_1_out), .sel(Branch));
  and and_1 (and_1_out, out_6[0], out_6[1]);
  dual_port_ram dual_port_ram_1 (
    .addr(addr), .pc(multiplexer_1_out), .d(d), .w(and_1_out), .clk(clk), .instr(out_6), .data(out_7));
endmodule

module dual_port_ram (
  input  [7:0] addr,
  input  [7:0] pc,
  input  [7:0] d,
  input  w,
  input  clk,
  output [7:0] instr,
  output [7:0] data
);

  wire or_1_out;
  wire [7:0] multiplexer_1_out;

  or or_1 (or_1_out, w, clk);
  Multiplexer #(.width(8)) multiplexer_1 (.in0(addr), .in1(pc), .out(multiplexer_1_out), .sel(clk));
  RAM #(.asyncread("true")) ram_1 (.addr(multiplexer_1_out), .we(or_1_out), .oe(1'b1), .clk(clk), .din(d), .dout(data));
  Register #(.trigger("falling")) pcbuf (.D(data), .en(1'b1), .clk(clk), .Q(instr));  // open: clr
endmodule

module banco_de_registradores (
  input  [7:0] Dado,
  input  Reset,
  input  RegWrite,
  input  [1:0] rs2,
  input  [1:0] rs1,
  input  ALUSrc,
  input  clk,
  output [7:0] saida_2,
  output [7:0] saida_1
);

  wire demultiplexer_1_out0, demultiplexer_1_out1, demultiplexer_1_out2, demultiplexer_1_out3;
  wire [1:0] rs1_t;
  wire [7:0] multiplexer_1_out, multiplexer_2_out, multiplexer_3_out, multiplexer_4_out, r0, r1, r2, r3;

  Demultiplexer #(.select(2)) demultiplexer_1 (
    .out0(demultiplexer_1_out0), .out1(demultiplexer_1_out1), .out2(demultiplexer_1_out2),
    .out3(demultiplexer_1_out3), .in(RegWrite), .sel(rs1_t));
  Multiplexer #(.width(8)) multiplexer_1 (.in0(r0), .in1(Dado), .out(multiplexer_1_out), .sel(demultiplexer_1_out0));
  Multiplexer #(.width(8)) multiplexer_2 (.in0(r1), .in1(Dado), .out(multiplexer_2_out), .sel(demultiplexer_1_out1));
  Multiplexer #(.width(8)) multiplexer_3 (.in0(r2), .in1(Dado), .out(multiplexer_3_out), .sel(demultiplexer_1_out2));
  Multiplexer #(.width(8)) multiplexer_4 (.in0(r3), .in1(Dado), .out(multiplexer_4_out), .sel(demultiplexer_1_out3));
  Register u_r0 (.D(multiplexer_1_out), .clk(clk), .Q(r0), .clr(Reset));  // open: en
  Register u_r1 (.D(multiplexer_2_out), .clk(clk), .Q(r1), .clr(Reset));  // open: en
  Register u_r2 (.D(multiplexer_3_out), .clk(clk), .Q(r2), .clr(Reset));  // open: en
  Register u_r3 (.D(multiplexer_4_out), .clk(clk), .Q(r3), .clr(Reset));  // open: en
  Multiplexer #(.select(2), .width(8)) multiplexer_5 (.in0(r0), .in1(r1), .in2(r2), .in3(r3), .out(saida_2), .sel(rs2));
  Multiplexer #(.select(2), .width(8)) multiplexer_6 (.in0(r0), .in1(r1), .in2(r2), .in3(r3), .out(saida_1), .sel(rs1));
  Multiplexer #(.width(2)) multiplexer_7 (.in0(rs1), .in1(2'b00), .out(rs1_t), .sel(ALUSrc));

  // Other names for the same wires on the sheet: D[7:0] = Dado
endmodule

module ULA (
  input  [7:0] rs2,
  input  [7:0] rs1,
  input  [1:0] ALUOp,
  output zero,
  output [7:0] out_5
);

  wire [7:0] adder_1_out, subtractor_1_out, undriven;

  Adder adder_1 (.a(rs1), .b(rs2), .out(adder_1_out));  // open: cin, cout
  Subtractor subtractor_1 (.a(rs1), .b(rs2), .out(subtractor_1_out));  // open: bin, bout
  Multiplexer #(.select(2), .width(8)) multiplexer_1 (
    .in0(adder_1_out), .in1(subtractor_1_out), .in2(undriven), .out(out_5), .sel(ALUOp));  // open: in3
  Comparator comparator_1 (.a({8{1'b0}}), .b(out_5), .eq(zero));  // open: gt, lt
endmodule

module unidade_de_controle (
  input  [3:0] in_1,
  output [1:0] ALUOp,
  output ALUSrc,
  output Branch,
  output RegWr,
  output MemtoReg
);

  wire and_1_out, and_2_out, and_5_out, not_1_out, not_3_out, not_4_out;

  not not_1 (not_1_out, in_1[3]);
  not not_2 (MemtoReg, in_1[2]);
  not not_3 (not_3_out, in_1[1]);
  not not_4 (not_4_out, in_1[0]);
  and and_1 (and_1_out, not_4_out, not_3_out, MemtoReg, not_1_out);
  and and_2 (and_2_out, in_1[3], in_1[2], not_3_out, in_1[0]);
  and and_3 (ALUSrc, in_1[2], not_1_out, not_3_out, not_4_out);
  and and_4 (Branch, not_3_out, MemtoReg);
  and and_5 (and_5_out, in_1[1], not_4_out);
  or or_1 (ALUOp[0], and_1_out, and_2_out);
  or or_2 (RegWr, and_5_out, in_1[2]);

  assign ALUOp[1] = 1'b0;
endmodule
