// Logisim project trabalho_2_pipeline.circ as structural Verilog: 9 circuits, main circuit PC_e_MI
module trabalho (
  output [7:0] out_1
);

  wire ALUSrc, and_1_out, Branch, clk, Incr, MemtoReg, not_1_out, not_2_out, PCSumSrc, RegWr, Reset_out, Zero;
  wire [1:0] pipeline1_1_out_8, pipeline1_1_out_9;
  wire [3:0] ALUOp, opcode, pc_e_mi_1_instr, pipeline1_1_out_10, pipeline1_1_out_11;
  wire [7:0] banco_de_registradores_1_saida_1, banco_de_registradores_1_saida_2, data, Imm,
       multiplexer_1_out, multiplexer_2_out, pipeline2_1_out_10, ra, rb, ula_1_out_7, undriven;

  and and_1 (and_1_out, Zero, Branch);
  not not_1 (not_1_out, clk);
  Clock clock_1 (.out(clk));
  PC_e_MI pc_e_mi_1 (
    .Imm(Imm), .PcSumSrc(PCSumSrc), .clk(not_1_out), .r2(rb), .Branch(and_1_out), .addr(rb), .d(ra),
    .out_10(out_1), .instr({opcode, pc_e_mi_1_instr}), .data(data));
  pipeline1 pipeline1_1 (
    .clk(clk), .rb(pc_e_mi_1_instr[1:0]), .ra(pc_e_mi_1_instr[3:2]), .imm(pc_e_mi_1_instr), .opcode(opcode),
    .PC(out_1), .out_8(pipeline1_1_out_8), .out_9(pipeline1_1_out_9), .out_10(pipeline1_1_out_10),
    .out_11(pipeline1_1_out_11), .out_7(out_1));
  Button Reset (.out(Reset_out));
  not not_2 (not_2_out, clk);
  assign Imm = {{4{pipeline1_1_out_10[3]}}, pipeline1_1_out_10};  // Bit_Extender bit_extender_1
  unidade_de_controle unidade_de_controle_1 (
    .opcode(pipeline1_1_out_11), .ALUSrc(ALUSrc), .Branch(Branch), .RegWr(RegWr), .MemtoReg(MemtoReg),
    .PcSumSrc(PCSumSrc), .Incr(Incr), .ALUOp(ALUOp));
  Multiplexer #(.width(8)) multiplexer_1 (.in0(undriven), .in1(data), .out(multiplexer_1_out), .sel(MemtoReg));
  banco_de_registradores banco_de_registradores_1 (
    .clk(not_2_out), .RegWrite(RegWr), .Dado(multiplexer_1_out), .Reset(Reset_out), .ALUSrc(ALUSrc),
    .rb(pipeline1_1_out_8), .ra(pipeline1_1_out_9), .saida_2(banco_de_registradores_1_saida_2),
    .saida_1(banco_de_registradores_1_saida_1));
  pipeline2 pipeline2_1 (
    .rb(banco_de_registradores_1_saida_2), .ra(banco_de_registradores_1_saida_1), .imm(Imm), .opcode(opcode),
    .PC(out_1), .clk(clk), .out_8(rb), .out_9(ra), .out_10(pipeline2_1_out_10), .out_11(opcode), .out_7(out_1));
  Multiplexer #(.width(8)) multiplexer_2 (.in0(rb), .in1(pipeline2_1_out_10), .out(multiplexer_2_out), .sel(ALUSrc));
  ULA ula_1 (
    .Branch(Branch), .Incr(Incr), .rb(multiplexer_2_out), .ra(ra), .ALUOp(ALUOp), .out_7(ula_1_out_7),
    .zero(Zero));
  pipeline3 pipeline3_1 (
    .clk(clk), .rULA(ula_1_out_7), .rb(rb), .opcode(opcode), .PC(out_1));  // open: TA, out_8, out_9, out_10, out_11, out_7

  // Other names for the same wires on the sheet: PC[7:0] = out_1
endmodule

module PC_e_MI (
  input  [7:0] addr,
  input  PcSumSrc,
  input  Branch,
  input  [7:0] Imm,
  input  [7:0] r2,
  input  clk,
  input  [7:0] d,
  output [7:0] instr,
  output [7:0] data,
  output [7:0] out_10
);

  wire and_1_out, button_1_out, not_1_out, not_2_out;
  wire [7:0] adder_1_out, multiplexer_1_out, multiplexer_2_out;

  Multiplexer #(.width(8)) multiplexer_1 (.in0(8'h1), .in1(Imm), .out(multiplexer_1_out), .sel(PcSumSrc));
  Adder adder_1 (.a(out_10), .b(multiplexer_1_out), .out(adder_1_out), .cin(1'b0));  // open: cout
  Multiplexer #(.width(8)) multiplexer_2 (.in0(adder_1_out), .in1(r2), .out(multiplexer_2_out), .sel(Branch));
  Register register_1 (.D(multiplexer_2_out), .en(1'b1), .clk(clk), .Q(out_10), .clr(button_1_out));
  Button button_1 (.out(button_1_out));
  not not_1 (not_1_out, instr[6]);
  not not_2 (not_2_out, instr[7]);
  and and_1 (and_1_out, instr[4], instr[5], not_1_out, not_2_out);
  dual_port_ram dual_port_ram_1 (.addr(addr), .pc(out_10), .d(d), .w(and_1_out), .clk(clk), .instr(instr), .data(data));
endmodule

module dual_port_ram (
  input  [7:0] addr,
  input  [7:0] pc,
  input  [7:0] d,
  input  w,
  input  clk,
  output [7:0] instr,
  output [7:0] data
);

  wire or_1_out;
  wire [7:0] multiplexer_1_out;

  or or_1 (or_1_out, w, clk);
  Multiplexer #(.width(8)) multiplexer_1 (.in0(addr), .in1(pc), .out(multiplexer_1_out), .sel(clk));
  RAM #(.asyncread("true")) ram_1 (.addr(multiplexer_1_out), .we(or_1_out), .oe(1'b1), .clk(clk), .din(d), .dout(data));
  Register #(.trigger("falling")) pcbuf (.D(data), .en(1'b1), .clk(clk), .Q(instr));  // open: clr
endmodule

module banco_de_registradores (
  input  Reset,
  input  [7:0] Dado,
  input  RegWrite,
  input  [1:0] rb,
  input  clk,
  input  [1:0] ra,
  input  ALUSrc,
  output [7:0] saida_2,
  output [7:0] saida_1
);

  wire demultiplexer_1_out0, demultiplexer_1_out1, demultiplexer_1_out2, demultiplexer_1_out3;
  wire [1:0] rd;
  wire [7:0] multiplexer_1_out, multiplexer_2_out, multiplexer_3_out, multiplexer_4_out, r0, r1, r2, r3;

  Demultiplexer #(.select(2)) demultiplexer_1 (
    .out0(demultiplexer_1_out0), .out1(demultiplexer_1_out1), .out2(demultiplexer_1_out2),
    .out3(demultiplexer_1_out3), .in(RegWrite), .sel(rd));
  Multiplexer #(.width(8)) multiplexer_1 (.in0(r0), .in1(Dado), .out(multiplexer_1_out), .sel(demultiplexer_1_out0));
  Multiplexer #(.width(8)) multiplexer_2 (.in0(r1), .in1(Dado), .out(multiplexer_2_out), .sel(demultiplexer_1_out1));
  Multiplexer #(.width(8)) multiplexer_3 (.in0(r2), .in1(Dado), .out(multiplexer_3_out), .sel(demultiplexer_1_out2));
  Multiplexer #(.width(8)) multiplexer_4 (.in0(r3), .in1(Dado), .out(multiplexer_4_out), .sel(demultiplexer_1_out3));
  Register u_r0 (.D(multiplexer_1_out), .clk(clk), .Q(r0), .clr(Reset));  // open: en
  Register u_r1 (.D(multiplexer_2_out), .clk(clk), .Q(r1), .clr(Reset));  // open: en
  Register u_r2 (.D(multiplexer_3_out), .clk(clk), .Q(r2), .clr(Reset));  // open: en
  Register u_r3 (.D(multiplexer_4_out), .clk(clk), .Q(r3), .clr(Reset));  // open: en
  Multiplexer #(.select(2), .width(8)) multiplexer_5 (.in0(r0), .in1(r1), .in2(r2), .in3(r3), .out(saida_2), .sel(rb));
  Multiplexer #(.select(2), .width(8)) multiplexer_6 (.in0(r0), .in1(r1), .in2(r2), .in3(r3), .out(saida_1), .sel(rd));
  Multiplexer #(.width(2)) multiplexer_7 (.in0(ra), .in1(2'b00), .out(rd), .sel(ALUSrc));

  // Other names for the same wires on the sheet: D[7:0] = Dado
endmodule

module ULA (
  input  [7:0] rb,
  input  [7:0] ra,
  input  Branch,
  input  Incr,
  input  [3:0] ALUOp,
  output zero,
  output [7:0] out_7
);

  wire Shift;
  wire [2:0] multiplexer_2_out;
  wire [4:0] multiplexer_2_out_2;
  wire [7:0] adder_1_out, and_1_out, multiplexer_1_out, multiplexer_3_out, multiplexer_4_out,
       multiplier_1_out, not_1_out, or_1_out, shifter_1_out, shifter_2_out, subtractor_1_out, xor_1_out;

  Multiplexer #(.width(8)) multiplexer_1 (.in0(rb), .in1({8{1'b0}}), .out(multiplexer_1_out), .sel(Branch));
  Multiplexer #(.width(8)) multiplexer_2 (
    .in0(multiplexer_1_out), .in1(8'h1), .out({multiplexer_2_out_2, multiplexer_2_out}), .sel(Incr));
  Comparator comparator_1 (.a({multiplexer_2_out_2, multiplexer_2_out}), .b(8'h7), .gt(Shift));  // open: eq, lt
  Shifter shifter_1 (.in(ra), .\dist (multiplexer_2_out), .out(shifter_1_out));
  Shifter #(.shift("lr")) shifter_2 (.in(ra), .\dist (multiplexer_2_out), .out(shifter_2_out));
  Adder adder_1 (.a(ra), .b({multiplexer_2_out_2, multiplexer_2_out}), .out(adder_1_out));  // open: cin, cout
  Subtractor subtractor_1 (
    .a(ra), .b({multiplexer_2_out_2, multiplexer_2_out}), .out(subtractor_1_out));  // open: bin, bout
  assign not_1_out = ~{multiplexer_2_out_2, multiplexer_2_out};  // NOT_Gate not_1, 8 bits wide
  assign and_1_out = ra & {multiplexer_2_out_2, multiplexer_2_out};  // AND_Gate and_1, 8 bits wide
  assign or_1_out = ra | {multiplexer_2_out_2, multiplexer_2_out};  // OR_Gate or_1, 8 bits wide
  assign xor_1_out = ra ^ {multiplexer_2_out_2, multiplexer_2_out};  // XOR_Gate xor_1, 8 bits wide
  Multiplexer #(.width(8)) multiplexer_3 (.in0(shifter_1_out), .in1({8{1'b0}}), .out(multiplexer_3_out), .sel(Shift));
  Multiplexer #(.width(8)) multiplexer_4 (.in0(shifter_2_out), .in1({8{1'b0}}), .out(multiplexer_4_out), .sel(Shift));
  Multiplier multiplier_1 (
    .a(ra), .b({multiplexer_2_out_2, multiplexer_2_out}), .out(multiplier_1_out));  // open: cin, cout
  Multiplexer #(.select(4), .width(8)) multiplexer_5 (
    .in0(adder_1_out), .in1(subtractor_1_out), .in2(not_1_out), .in3(and_1_out), .in4(or_1_out),
    .in5(xor_1_out), .in6(multiplexer_3_out), .in7(multiplexer_4_out), .in8(multiplier_1_out),
    .in9({multiplexer_2_out_2, multiplexer_2_out}), .out(out_7), .sel(ALUOp));  // open: in10, in11, in12, in13, in14, in15
  Comparator comparator_2 (.a({8{1'b0}}), .b(out_7), .eq(zero));  // open: gt, lt

  // Notes on the sheet:
  //   para (ra - 0)
  //   mv
endmodule

module unidade_de_controle (
  input  [3:0] opcode,
  output [3:0] ALUOp,
  output ALUSrc,
  output Branch,
  output RegWr,
  output MemtoReg,
  output PcSumSrc,
  output Incr
);

  wire and_1_out, and_2_out, and_4_out, and_5_out, and_6_out, and_7_out, and_8_out, and_11_out, not_1_out,
       not_2_out, not_3_out, not_4_out;

  not not_1 (not_1_out, opcode[3]);
  not not_2 (not_2_out, opcode[2]);
  not not_3 (not_3_out, opcode[1]);
  not not_4 (not_4_out, opcode[0]);
  and and_1 (and_1_out, not_1_out, opcode[2], not_3_out, opcode[0]);
  or or_1 (ALUOp[3], and_1_out, and_2_out);
  and and_2 (and_2_out, not_1_out, opcode[2], opcode[1], not_4_out);
  and and_3 (ALUOp[2], opcode[3], opcode[1]);
  and and_4 (and_4_out, opcode[3], not_2_out, not_3_out);
  or or_2 (ALUOp[1], and_4_out, and_5_out);
  and and_5 (and_5_out, opcode[3], opcode[2], opcode[1]);
  and and_6 (and_6_out, not_1_out, not_2_out, not_3_out, not_4_out);
  and and_7 (and_7_out, not_1_out, opcode[2], opcode[1], not_4_out);
  or or_3 (ALUOp[0], and_6_out, and_7_out, and_8_out);
  and and_8 (and_8_out, opcode[3], opcode[0]);
  and and_9 (ALUSrc, not_1_out, opcode[2], not_3_out);
  and and_10 (Branch, not_4_out, not_3_out, not_2_out, not_1_out);
  and and_11 (and_11_out, opcode[1], not_4_out);
  or or_4 (RegWr, and_11_out, opcode[2], opcode[3]);
  and and_12 (MemtoReg, not_1_out, not_2_out, opcode[1], not_4_out);
  and and_13 (PcSumSrc, not_1_out, not_2_out, not_3_out, opcode[0]);
  and and_14 (Incr, not_1_out, opcode[2], opcode[1], opcode[0]);
endmodule

module pipeline1 (
  input  [7:0] PC,
  input  clk,
  input  [1:0] rb,
  input  [1:0] ra,
  input  [3:0] imm,
  input  [3:0] opcode,
  output [7:0] out_7,
  output [1:0] out_8,
  output [1:0] out_9,
  output [3:0] out_10,
  output [3:0] out_11
);

  Register register_1 (.D(PC), .en(1'b1), .clk(clk), .Q(out_7));  // open: clr
  Register #(.width(2)) register_2 (.D(rb), .en(1'b1), .clk(clk), .Q(out_8));  // open: clr
  Register #(.width(2)) register_3 (.D(ra), .en(1'b1), .clk(clk), .Q(out_9));  // open: clr
  Register #(.width(4)) register_4 (.D(imm), .en(1'b1), .clk(clk), .Q(out_10));  // open: clr
  Register #(.width(4)) register_5 (.D(opcode), .en(1'b1), .clk(clk), .Q(out_11));  // open: clr
endmodule

module pipeline2 (
  input  [7:0] PC,
  input  clk,
  input  [7:0] rb,
  input  [7:0] ra,
  input  [7:0] imm,
  input  [3:0] opcode,
  output [7:0] out_7,
  output [7:0] out_8,
  output [7:0] out_9,
  output [7:0] out_10,
  output [3:0] out_11
);

  Register register_1 (.D(PC), .en(1'b1), .clk(clk), .Q(out_7));  // open: clr
  Register register_2 (.D(rb), .en(1'b1), .clk(clk), .Q(out_8));  // open: clr
  Register register_3 (.D(ra), .en(1'b1), .clk(clk), .Q(out_9));  // open: clr
  Register register_4 (.D(imm), .en(1'b1), .clk(clk), .Q(out_10));  // open: clr
  Register #(.width(4)) register_5 (.D(opcode), .en(1'b1), .clk(clk), .Q(out_11));  // open: clr
endmodule

module pipeline3 (
  input  [7:0] PC,
  input  clk,
  input  [7:0] TA,
  input  [7:0] rULA,
  input  [7:0] rb,
  input  [3:0] opcode,
  output [7:0] out_7,
  output [7:0] out_8,
  output [7:0] out_9,
  output [7:0] out_10,
  output [3:0] out_11
);

  Register register_1 (.D(PC), .en(1'b1), .clk(clk), .Q(out_7));  // open: clr
  Register register_2 (.D(TA), .en(1'b1), .clk(clk), .Q(out_8));  // open: clr
  Register register_3 (.D(rULA), .en(1'b1), .clk(clk), .Q(out_9));  // open: clr
  Register register_4 (.D(rb), .en(1'b1), .clk(clk), .Q(out_10));  // open: clr
  Register #(.width(4)) register_5 (.D(opcode), .en(1'b1), .clk(clk), .Q(out_11));  // open: clr
endmodule
