// Logisim project trabalho_3.circ as structural Verilog: 14 circuits, main circuit PC_e_MI
module trabalho (
  output [7:0] out_1
);

  wire ALUOp_1, ALUOp_3, ALUSrc, ALUSrc_1, ALUSrc_2, Branch, button_1_out, button_2_out, clk, Incr, Jump,
       MemtoReg, MemWr, not_1_out, PcSrc, RegWr, RegWr_1, RegWr_3, RegWr_4, Zero, zero_1, zero_2, zero_3,
       zero_4;
  wire [1:0] ALUOp_2;
  wire [2:0] ALUOp_4;
  wire [3:0] ALUOp, banco_de_registradores_2_p3, op1, op2, op3, op4, undriven;
  wire [7:0] adder_1_out, data, Imm, multiplexer_1_out, multiplexer_2_out, multiplexer_3_out,
       multiplexer_4_out, ra, ra_1, ra_2, ra_3, ra_4, rb, rb_1, rb_2, rb_3, rb_4, rULA_1, rULA_2, rULA_3,
       rULA_4, TA, ula_1_out_7;
  wire [27:0] pc_e_mi_1_instr;

  Adder adder_1 (.a(out_1), .b(8'h1), .out(adder_1_out), .cin(1'b0));  // open: cout
  Multiplexer #(.width(8)) multiplexer_1 (.in0(adder_1_out), .in1(TA), .out(multiplexer_1_out), .sel(PcSrc));
  not not_1 (not_1_out, clk);
  Clock clock_1 (.out(clk));
  PC_e_MI pc_e_mi_1 (
    .clk(not_1_out), .PC(multiplexer_1_out), .d(ra_1), .MemWr(MemWr), .addr(rb_1), .out_7(out_1),
    .instr({op1, pc_e_mi_1_instr[27:24], op2, pc_e_mi_1_instr[19:16], op3, pc_e_mi_1_instr[11:8], op4, pc_e_mi_1_instr[3:0]}),
    .data(data));
  unidade_de_controle_1 unidade_de_controle_1_1 (
    .opcode(op1), .MemtoReg(MemtoReg), .RegWr(RegWr_1), .ALUSrc(ALUSrc_1), .ALUOp(ALUOp_1), .MemWr(MemWr));
  unidade_de_controle_3 unidade_de_controle_3_1 (.opcode(op3), .ALUOp(ALUOp_3), .RegWr(RegWr_3));
  unidade_de_controle_2 unidade_de_controle_2_1 (
    .opcode(op2), .Branch(Branch), .ALUSrc(ALUSrc_2), .ALUOp(ALUOp_2), .Jump(Jump));
  unidade_de_controle_4 unidade_de_controle_4_1 (.opcode(op4), .ALUOp(ALUOp_4), .RegWr(RegWr_4));
  Multiplexer #(.width(8)) multiplexer_2 (.in0(rULA_1), .in1(data), .out(multiplexer_2_out), .sel(MemtoReg));
  Button button_1 (.out(button_1_out));
  banco_de_registradores banco_de_registradores_1 (
    .Reset(button_1_out), .ALUSrc_1(ALUSrc_1), .ALUSrc_2(ALUSrc_2), .RegWr_1(RegWr_1), .RegWr_3(RegWr_3),
    .RegWr_4(RegWr_4), .clk(clk), .rb_1(pc_e_mi_1_instr[25:24]), .rb_4(pc_e_mi_1_instr[1:0]),
    .ra_4(pc_e_mi_1_instr[3:2]), .rb_2(pc_e_mi_1_instr[17:16]), .rb_3(pc_e_mi_1_instr[9:8]),
    .ra_3(pc_e_mi_1_instr[11:10]), .ra_1(pc_e_mi_1_instr[27:26]), .ra_2(pc_e_mi_1_instr[19:18]),
    .Dado_1(multiplexer_2_out), .Dado_2(rULA_3), .Dado_3(rULA_4), .saida_rb_4(rb_4), .saida_ra_4(ra_4),
    .saida_ra_1(ra_1), .saida_rb_2(rb_2), .saida_ra_2(ra_2), .saida_rb_1(rb_1), .saida_rb_3(rb_3),
    .saida_ra_3(ra_3));
  ULA_4 ula_4_1 (.rb(rb_4), .ra(ra_4), .ALUOp(ALUOp_4), .zero(zero_4), .out_5(rULA_4));
  ULA_3 ula_3_1 (.rb(rb_3), .ra(ra_3), .zero(zero_3), .out_5(rULA_3));  // open: ALUOp
  ULA_2 ula_2_1 (.ra(ra_2), .zero(zero_2), .out_3(rULA_2));
  ULA_1 ula_1_1 (.rb(rb_1), .ra(ra_1), .ALUOp(ALUOp_1), .zero(zero_1), .out_5(rULA_1));
  Button button_2 (.out(button_2_out));
  // NOT_Gate not_2 has open pins: in=clk, out=open
  Multiplexer #(.width(8)) multiplexer_3 (.in0(ula_1_out_7), .in1(data), .out(multiplexer_3_out), .sel(MemtoReg));
  assign Imm = {{4{undriven[3]}}, undriven};  // Bit_Extender bit_extender_1
  // banco_de_registradores banco_de_registradores_2: pin names not known; wires that end beside it: button_2_out, RegWr, banco_de_registradores_2_p3[1:0], banco_de_registradores_2_p3[3:2], ALUSrc, multiplexer_3_out, rb, ra
  Multiplexer #(.width(8)) multiplexer_4 (.in0(rb), .in1(Imm), .out(multiplexer_4_out), .sel(ALUSrc));
  ULA ula_1 (
    .Branch(Branch), .Incr(Incr), .rb(multiplexer_4_out), .ra(ra), .ALUOp(ALUOp), .out_7(ula_1_out_7),
    .zero(Zero));

  // Other names for the same wires on the sheet: PC[7:0] = out_1

  // Notes on the sheet:
  //   Reset
endmodule

module PC_e_MI (
  input  [7:0] addr,
  input  [7:0] PC,
  input  clk,
  input  MemWr,
  input  [7:0] d,
  output [31:0] instr,
  output [7:0] out_7,
  output [7:0] data
);

  wire button_1_out;
  wire [31:0] bit_extender_1_out;
  wire [31:8] dual_port_ram_1_data;

  Register register_1 (.D(PC), .en(1'b1), .clk(clk), .Q(out_7), .clr(button_1_out));
  Button button_1 (.out(button_1_out));
  assign bit_extender_1_out = {{24{1'b0}}, d};  // Bit_Extender bit_extender_1
  dual_port_ram dual_port_ram_1 (
    .addr(addr), .pc(out_7), .d(bit_extender_1_out), .w(MemWr), .clk(clk), .instr(instr),
    .data({dual_port_ram_1_data, data}));
endmodule

module dual_port_ram (
  input  [7:0] addr,
  input  [7:0] pc,
  input  [31:0] d,
  input  w,
  input  clk,
  output [31:0] instr,
  output [31:0] data
);

  wire or_1_out;
  wire [7:0] multiplexer_1_out;

  Multiplexer #(.width(8)) multiplexer_1 (.in0(addr), .in1(pc), .out(multiplexer_1_out), .sel(clk));
  RAM #(.asyncread("true"), .dataWidth(32)) ram_1 (
    .addr(multiplexer_1_out), .we(or_1_out), .oe(1'b1), .clk(clk), .din(d), .dout(data));
  or or_1 (or_1_out, w, clk);
  Register #(.trigger("falling"), .width(32)) pcbuf (.D(data), .en(1'b1), .clk(clk), .Q(instr));  // open: clr
endmodule

module banco_de_registradores (
  input  [1:0] rb_1,
  input  [1:0] ra_1,
  input  Reset,
  input  [7:0] Dado_1,
  input  [7:0] Dado_2,
  input  [1:0] rb_2,
  input  [7:0] Dado_3,
  input  ALUSrc_1,
  input  [1:0] ra_2,
  input  ALUSrc_2,
  input  RegWr_1,
  input  RegWr_3,
  input  RegWr_4,
  input  [1:0] rb_3,
  input  clk,
  input  [1:0] ra_3,
  input  [1:0] rb_4,
  input  [1:0] ra_4,
  output [7:0] saida_rb_1,
  output [7:0] saida_ra_1,
  output [7:0] saida_rb_2,
  output [7:0] saida_ra_2,
  output [7:0] saida_rb_3,
  output [7:0] saida_ra_3,
  output [7:0] saida_rb_4,
  output [7:0] saida_ra_4
);

  wire comparator_1_eq, comparator_2_eq, comparator_3_eq, comparator_4_eq, comparator_5_eq, comparator_6_eq,
       comparator_7_eq, comparator_8_eq, comparator_9_eq, comparator_10_eq, comparator_11_eq,
       comparator_12_eq, l1_0, l1_1, l1_2, l1_3, l2_0, l2_1, l2_2, l2_3, l3_0, l3_1, l3_2, l3_3, or_1_out,
       or_2_out, or_3_out, or_4_out;
  wire [1:0] or_5_out, or_7_out, or_9_out, or_11_out, rd_1, rd_2;
  wire [7:0] multiplexer_1_out, multiplexer_2_out, multiplexer_3_out, multiplexer_4_out, r0, r1, r2, r3;

  and and_1 (l1_0, RegWr_1, comparator_1_eq);
  Comparator #(.width(2)) comparator_1 (.a(rd_1), .b(2'b00), .eq(comparator_1_eq));  // open: gt, lt
  and and_2 (l2_0, RegWr_3, comparator_2_eq);
  Comparator #(.width(2)) comparator_2 (.a(ra_3), .b(2'b00), .eq(comparator_2_eq));  // open: gt, lt
  and and_3 (l3_0, RegWr_4, comparator_3_eq);
  Comparator #(.width(2)) comparator_3 (.a(ra_4), .b(2'b00), .eq(comparator_3_eq));  // open: gt, lt
  and and_4 (l1_1, RegWr_1, comparator_4_eq);
  Comparator #(.width(2)) comparator_4 (.a(rd_1), .b(2'b01), .eq(comparator_4_eq));  // open: gt, lt
  and and_5 (l2_1, RegWr_3, comparator_5_eq);
  Comparator #(.width(2)) comparator_5 (.a(ra_3), .b(2'b01), .eq(comparator_5_eq));  // open: gt, lt
  and and_6 (l3_1, RegWr_4, comparator_6_eq);
  Comparator #(.width(2)) comparator_6 (.a(ra_4), .b(2'b01), .eq(comparator_6_eq));  // open: gt, lt
  and and_7 (l1_2, RegWr_1, comparator_7_eq);
  Comparator #(.width(2)) comparator_7 (.a(rd_1), .b(2'b10), .eq(comparator_7_eq));  // open: gt, lt
  and and_8 (l2_2, RegWr_3, comparator_8_eq);
  Comparator #(.width(2)) comparator_8 (.a(ra_3), .b(2'b10), .eq(comparator_8_eq));  // open: gt, lt
  and and_9 (l3_2, RegWr_4, comparator_9_eq);
  Comparator #(.width(2)) comparator_9 (.a(ra_4), .b(2'b10), .eq(comparator_9_eq));  // open: gt, lt
  and and_10 (l1_3, RegWr_1, comparator_10_eq);
  Comparator #(.width(2)) comparator_10 (.a(rd_1), .b(2'b11), .eq(comparator_10_eq));  // open: gt, lt
  and and_11 (l2_3, RegWr_3, comparator_11_eq);
  Comparator #(.width(2)) comparator_11 (.a(ra_3), .b(2'b11), .eq(comparator_11_eq));  // open: gt, lt
  and and_12 (l3_3, RegWr_4, comparator_12_eq);
  Comparator #(.width(2)) comparator_12 (.a(ra_4), .b(2'b11), .eq(comparator_12_eq));  // open: gt, lt
  or or_1 (or_1_out, l1_0, l2_0, l3_0);
  or or_2 (or_2_out, l1_1, l2_1, l3_1);
  or or_3 (or_3_out, l1_2, l2_2, l3_2);
  or or_4 (or_4_out, l1_3, l2_3, l3_3);
  or or_5 (or_5_out[0], l1_0, l3_0);
  or or_6 (or_5_out[1], l2_0, l3_0);
  or or_7 (or_7_out[0], l1_1, l3_1);
  or or_8 (or_7_out[1], l2_1, l3_1);
  or or_9 (or_9_out[0], l1_2, l3_2);
  or or_10 (or_9_out[1], l2_2, l3_2);
  or or_11 (or_11_out[0], l1_3, l3_3);
  or or_12 (or_11_out[1], l2_3, l3_3);
  Multiplexer #(.select(2), .width(8)) multiplexer_1 (
    .in1(Dado_1), .in2(Dado_2), .in3(Dado_3), .out(multiplexer_1_out), .sel(or_5_out));  // open: in0
  Multiplexer #(.select(2), .width(8)) multiplexer_2 (
    .in1(Dado_1), .in2(Dado_2), .in3(Dado_3), .out(multiplexer_2_out), .sel(or_7_out));  // open: in0
  Multiplexer #(.select(2), .width(8)) multiplexer_3 (
    .in1(Dado_1), .in2(Dado_2), .in3(Dado_3), .out(multiplexer_3_out), .sel(or_9_out));  // open: in0
  Multiplexer #(.select(2), .width(8)) multiplexer_4 (
    .in1(Dado_1), .in2(Dado_2), .in3(Dado_3), .out(multiplexer_4_out), .sel(or_11_out));  // open: in0
  Register u_r3 (.D(multiplexer_4_out), .en(or_4_out), .clk(clk), .Q(r3), .clr(Reset));
  Register u_r0 (.D(multiplexer_1_out), .en(or_1_out), .clk(clk), .Q(r0), .clr(Reset));
  Register u_r1 (.D(multiplexer_2_out), .en(or_2_out), .clk(clk), .Q(r1), .clr(Reset));
  Register u_r2 (.D(multiplexer_3_out), .en(or_3_out), .clk(clk), .Q(r2), .clr(Reset));
  Multiplexer #(.select(2), .width(8)) multiplexer_5 (
    .in0(r0), .in1(r1), .in2(r2), .in3(r3), .out(saida_rb_1), .sel(rb_1));
  Multiplexer #(.select(2), .width(8)) multiplexer_6 (
    .in0(r0), .in1(r1), .in2(r2), .in3(r3), .out(saida_ra_1), .sel(rd_1));
  Multiplexer #(.width(2)) multiplexer_7 (.in0(ra_1), .in1(2'b00), .out(rd_1), .sel(ALUSrc_1));
  Multiplexer #(.select(2), .width(8)) multiplexer_8 (
    .in0(r0), .in1(r1), .in2(r2), .in3(r3), .out(saida_rb_2), .sel(rb_2));
  Multiplexer #(.select(2), .width(8)) multiplexer_9 (
    .in0(r0), .in1(r1), .in2(r2), .in3(r3), .out(saida_ra_2), .sel(rd_2));
  Multiplexer #(.width(2)) multiplexer_10 (.in0(ra_2), .in1(2'b00), .out(rd_2), .sel(ALUSrc_2));
  Multiplexer #(.select(2), .width(8)) multiplexer_11 (
    .in0(r0), .in1(r1), .in2(r2), .in3(r3), .out(saida_rb_3), .sel(rb_3));
  Multiplexer #(.select(2), .width(8)) multiplexer_12 (
    .in0(r0), .in1(r1), .in2(r2), .in3(r3), .out(saida_ra_3), .sel(ra_3));
  Multiplexer #(.select(2), .width(8)) multiplexer_13 (
    .in0(r0), .in1(r1), .in2(r2), .in3(r3), .out(saida_rb_4), .sel(rb_4));
  Multiplexer #(.select(2), .width(8)) multiplexer_14 (
    .in0(r0), .in1(r1), .in2(r2), .in3(r3), .out(saida_ra_4), .sel(ra_4));

  // Other names for the same wires on the sheet: D1[7:0] = Dado_1; D2[7:0] = Dado_2; D3[7:0] = Dado_3;
  //   rd_3[1:0] = ra_3; rd_4[1:0] = ra_4
endmodule

module ULA (
  input  [7:0] rb,
  input  [7:0] ra,
  input  Branch,
  input  Incr,
  input  [3:0] ALUOp,
  output zero,
  output [7:0] out_7
);

  wire Shift;
  wire [2:0] multiplexer_2_out;
  wire [4:0] multiplexer_2_out_2;
  wire [7:0] adder_1_out, and_1_out, multiplexer_1_out, multiplexer_3_out, multiplexer_4_out,
       multiplier_1_out, not_1_out, or_1_out, shifter_1_out, shifter_2_out, subtractor_1_out, undriven,
       xor_1_out;

  Multiplexer #(.width(8)) multiplexer_1 (.in0(rb), .in1({8{1'b0}}), .out(multiplexer_1_out), .sel(Branch));
  Multiplexer #(.width(8)) multiplexer_2 (
    .in0(multiplexer_1_out), .in1(8'h1), .out({multiplexer_2_out_2, multiplexer_2_out}), .sel(Incr));
  Comparator comparator_1 (.a({multiplexer_2_out_2, multiplexer_2_out}), .b(8'h7), .gt(Shift));  // open: eq, lt
  Shifter shifter_1 (.in(ra), .\dist (multiplexer_2_out), .out(shifter_1_out));
  Shifter #(.shift("lr")) shifter_2 (.in(ra), .\dist (multiplexer_2_out), .out(shifter_2_out));
  Adder adder_1 (.a(ra), .b({multiplexer_2_out_2, multiplexer_2_out}), .out(adder_1_out));  // open: cin, cout
  Subtractor subtractor_1 (
    .a(ra), .b({multiplexer_2_out_2, multiplexer_2_out}), .out(subtractor_1_out));  // open: bin, bout
  assign not_1_out = ~{multiplexer_2_out_2, multiplexer_2_out};  // NOT_Gate not_1, 8 bits wide
  assign and_1_out = ra & {multiplexer_2_out_2, multiplexer_2_out};  // AND_Gate and_1, 8 bits wide
  assign or_1_out = ra | {multiplexer_2_out_2, multiplexer_2_out};  // OR_Gate or_1, 8 bits wide
  assign xor_1_out = ra ^ {multiplexer_2_out_2, multiplexer_2_out};  // XOR_Gate xor_1, 8 bits wide
  Multiplexer #(.width(8)) multiplexer_3 (.in0(shifter_1_out), .in1({8{1'b0}}), .out(multiplexer_3_out), .sel(Shift));
  Multiplexer #(.width(8)) multiplexer_4 (.in0(shifter_2_out), .in1({8{1'b0}}), .out(multiplexer_4_out), .sel(Shift));
  Multiplier multiplier_1 (
    .a(ra), .b({multiplexer_2_out_2, multiplexer_2_out}), .out(multiplier_1_out));  // open: cin, cout
  Multiplexer #(.select(4), .width(8)) multiplexer_5 (
    .in0(adder_1_out), .in1(subtractor_1_out), .in2(not_1_out), .in3(and_1_out), .in4(or_1_out),
    .in5(xor_1_out), .in6(multiplexer_3_out), .in7(multiplexer_4_out), .in8(multiplier_1_out),
    .in9({multiplexer_2_out_2, multiplexer_2_out}), .in10(undriven), .out(out_7), .sel(ALUOp));  // open: in11, in12, in13, in14, in15
  Comparator comparator_2 (.a({8{1'b0}}), .b(out_7), .eq(zero));  // open: gt, lt

  // Notes on the sheet:
  //   para (ra - 0)
  //   mv
endmodule

module unidade_de_controle (
  input  [3:0] opcode,
  output [3:0] ALUOp,
  output ALUSrc,
  output Branch,
  output RegWr,
  output MemtoReg,
  output PcSumSrc,
  output Incr
);

  wire and_1_out, and_2_out, and_4_out, and_5_out, and_6_out, and_7_out, and_8_out, and_11_out, not_1_out,
       not_2_out, not_3_out, not_4_out;

  not not_1 (not_1_out, opcode[3]);
  not not_2 (not_2_out, opcode[2]);
  not not_3 (not_3_out, opcode[1]);
  not not_4 (not_4_out, opcode[0]);
  and and_1 (and_1_out, not_1_out, opcode[2], not_3_out, opcode[0]);
  or or_1 (ALUOp[3], and_1_out, and_2_out);
  and and_2 (and_2_out, not_1_out, opcode[2], opcode[1], not_4_out);
  and and_3 (ALUOp[2], opcode[3], opcode[1]);
  and and_4 (and_4_out, opcode[3], not_2_out, not_3_out);
  or or_2 (ALUOp[1], and_4_out, and_5_out);
  and and_5 (and_5_out, opcode[3], opcode[2], opcode[1]);
  and and_6 (and_6_out, not_1_out, not_2_out, not_3_out, not_4_out);
  and and_7 (and_7_out, not_1_out, opcode[2], opcode[1], not_4_out);
  or or_3 (ALUOp[0], and_6_out, and_7_out, and_8_out);
  and and_8 (and_8_out, opcode[3], opcode[0]);
  and and_9 (ALUSrc, not_1_out, opcode[2], not_3_out);
  and and_10 (Branch, not_4_out, not_3_out, not_2_out, not_1_out);
  and and_11 (and_11_out, opcode[1], not_4_out);
  or or_4 (RegWr, and_11_out, opcode[2], opcode[3]);
  and and_12 (MemtoReg, not_1_out, not_2_out, opcode[1], not_4_out);
  and and_13 (PcSumSrc, not_1_out, not_2_out, not_3_out, opcode[0]);
  and and_14 (Incr, not_1_out, opcode[2], opcode[1], opcode[0]);
endmodule

module unidade_de_controle_1 (
  input  [3:0] opcode,
  output MemWr,
  output MemtoReg,
  output RegWr,
  output ALUSrc,
  output ALUOp
);

  wire and_3_out, and_4_out, not_1_out, not_2_out, not_3_out;

  not not_1 (not_1_out, opcode[3]);
  not not_2 (not_2_out, opcode[1]);
  not not_3 (not_3_out, opcode[0]);
  and and_1 (MemWr, not_1_out, opcode[2], not_2_out, opcode[0]);
  and and_2 (MemtoReg, not_1_out, opcode[2], not_2_out, not_3_out);
  and and_3 (and_3_out, not_1_out, opcode[2], not_3_out);
  and and_4 (and_4_out, not_1_out, opcode[2], opcode[1]);
  and and_5 (ALUSrc, not_1_out, opcode[2], opcode[1]);
  and and_6 (ALUOp, not_1_out, opcode[2], opcode[0]);
  or or_1 (RegWr, and_3_out, and_4_out);
endmodule

module unidade_de_controle_2 (
  input  [3:0] opcode,
  output Jump,
  output Branch,
  output ALUSrc,
  output [1:0] ALUOp
);

  not not_1 (Branch, opcode[1]);

  assign ALUOp = opcode[1:0];
  assign ALUSrc = opcode[0];
  assign Jump = opcode[1];
endmodule

module unidade_de_controle_3 (
  input  [3:0] opcode,
  output RegWr,
  output ALUOp
);


  assign ALUOp = opcode[0];
  assign RegWr = 1'b1;
endmodule

module unidade_de_controle_4 (
  input  [3:0] opcode,
  output RegWr,
  output [2:0] ALUOp
);

  wire not_1_out, not_3_out;

  not not_1 (not_1_out, opcode[2]);
  not not_2 (ALUOp[1], opcode[1]);
  not not_3 (not_3_out, opcode[0]);
  or or_1 (RegWr, not_1_out, ALUOp[1], not_3_out);
  and and_1 (ALUOp[2], opcode[1], not_3_out);

  assign ALUOp[0] = opcode[0];
endmodule

module ULA_1 (
  input  [7:0] rb,
  input  [7:0] ra,
  input  ALUOp,
  output zero,
  output [7:0] out_5
);

  Multiplexer #(.width(8)) multiplexer_1 (.in0({rb[3:0], ra[3:0]}), .in1({ra[7:4], rb[3:0]}), .out(out_5), .sel(ALUOp));
  Comparator comparator_1 (.a({8{1'b0}}), .b(out_5), .eq(zero));  // open: gt, lt
endmodule

module ULA_2 (
  input  [7:0] ra,
  output zero,
  output [7:0] out_3
);

  Subtractor subtractor_1 (.a(ra), .b({8{1'b0}}), .out(out_3));  // open: bin, bout
  Comparator comparator_1 (.a({8{1'b0}}), .b(out_3), .eq(zero));  // open: gt, lt
endmodule

module ULA_3 (
  input  [7:0] rb,
  input  [7:0] ra,
  input  ALUOp,
  output zero,
  output [7:0] out_5
);

  wire [7:0] adder_1_out, subtractor_1_out;

  Adder adder_1 (.a(ra), .b(rb), .out(adder_1_out));  // open: cin, cout
  Subtractor subtractor_1 (.a(ra), .b(rb), .out(subtractor_1_out));  // open: bin, bout
  Multiplexer #(.width(8)) multiplexer_1 (.in0(adder_1_out), .in1(subtractor_1_out), .out(out_5), .sel(ALUOp));
  Comparator comparator_1 (.a({8{1'b0}}), .b(out_5), .eq(zero));  // open: gt, lt
endmodule

module ULA_4 (
  input  [7:0] rb,
  input  [7:0] ra,
  input  [2:0] ALUOp,
  output zero,
  output [7:0] out_5
);

  wire comparator_2_eq, Shift;
  wire [7:0] bit_extender_1_out, multiplexer_1_out, multiplexer_2_out, or_1_out, shifter_1_out, shifter_2_out;

  Comparator comparator_1 (.a(rb), .b(8'h7), .gt(Shift));  // open: eq, lt
  assign or_1_out = ra | rb;  // OR_Gate or_1, 8 bits wide
  Comparator comparator_2 (.a(rb), .b({8{1'b0}}), .eq(comparator_2_eq));  // open: gt, lt
  Shifter shifter_1 (.in(ra), .\dist (rb[2:0]), .out(shifter_1_out));
  Shifter #(.shift("lr")) shifter_2 (.in(ra), .\dist (rb[2:0]), .out(shifter_2_out));
  assign bit_extender_1_out = {{7{1'b0}}, comparator_2_eq};  // Bit_Extender bit_extender_1
  Multiplexer #(.width(8)) multiplexer_1 (.in0(shifter_1_out), .in1({8{1'b0}}), .out(multiplexer_1_out), .sel(Shift));
  Multiplexer #(.width(8)) multiplexer_2 (.in0(shifter_2_out), .in1({8{1'b0}}), .out(multiplexer_2_out), .sel(Shift));
  Multiplexer #(.select(3), .width(8)) multiplexer_3 (
    .in0(or_1_out), .in1(bit_extender_1_out), .in2(multiplexer_1_out), .in3(multiplexer_2_out), .out(out_5),
    .sel(ALUOp));  // open: in4, in5, in6, in7
  Comparator comparator_3 (.a({8{1'b0}}), .b(out_5), .eq(zero));  // open: gt, lt
endmodule
